# Fritzing sketch Layout (saved by Fritzing 0.9.5d)
breadboards: 1

parts:
  Q1 = TRANSISTOR_NPN [package=to-92]
  Eheim_Motor = DC Motor
  part = ESP32-38PinWide [part_number=ESP32-38PinWide]
  Contact_Sensor = SWITCH-MOMENTARY-2 [package=tactile_switch_smd]

nets:
  N1: Q1.E, Eheim_Motor.pin_1
  N2: Q1.B, part.GPIO22
  N3: Q1.C, part.3.3
  N4: Eheim_Motor.pin_2, part.GND, Contact_Sensor.2
  N5: part.GPIO23, Contact_Sensor.1

custom parts:
  ESP32-38PinWide: Generic 38-Pin ESP32 with wide format (only access to one side of pins on a breadboard) based on Stephen Lilley's HiLetgo ESP-WROOM-32 ESP32 ESP-32S Development Board.
